// Logisim project single cycle.circ as structural Verilog: 13 circuits, main circuit main
module main (
);

  wire branch_alu_1_out_4, button_1_out, clock_1_out, contrl_decoder_1_out_4, contrl_decoder_1_out_5,
       contrl_decoder_1_out_6, contrl_decoder_1_out_7, contrl_decoder_1_out_8, contrl_decoder_1_out_12;
  wire [1:0] contrl_decoder_1_out_3, contrl_decoder_1_out_9, contrl_decoder_1_out_10;
  wire [2:0] contrl_decoder_1_out_11;
  wire [3:0] alu_controller_1_out_4;
  wire [31:0] adder_1_out, immigiate_1_out_4, immigiate_1_out_5, immigiate_1_out_6, multiplexer_1_out,
       multiplexer_2_out, multiplexer_3_out, multiplexer_4_out, multiplexer_5_out, n32_bit_alu_1_out_4,
       ram_1_data, reg_file_1_read_data1, reg_file_1_read_data_2, register_1_q, rom_1_data;

  Multiplexer #(.select(2), .width(32)) multiplexer_1 (
    .in0(adder_1_out), .in1(immigiate_1_out_5), .in2(immigiate_1_out_6), .in3(n32_bit_alu_1_out_4),
    .out(multiplexer_1_out), .sel(contrl_decoder_1_out_9));  // open: en
  Clock clock_1 (.out(clock_1_out));
  Register #(.width(32)) register_1 (
    .D(multiplexer_1_out), .Q(register_1_q), .clk(clock_1_out), .clr(button_1_out));  // open: en
  Button button_1 (.out(button_1_out));
  Adder #(.width(32)) adder_1 (.a(register_1_q), .b(32'h4), .out(adder_1_out));  // open: cin, cout
  ROM #(.addrWidth(10), .dataWidth(32)) rom_1 (.addr(register_1_q[11:2]), .data(rom_1_data));  // open: sel
  immigiate immigiate_1 (
    .in_1(rom_1_data), .in_3(register_1_q), .out_4(immigiate_1_out_4), .out_5(immigiate_1_out_5),
    .out_6(immigiate_1_out_6), .in_2(contrl_decoder_1_out_10));
  contrl_decoder contrl_decoder_1 (
    .in_1(rom_1_data[6:0]), .in_2(branch_alu_1_out_4), .out_3(contrl_decoder_1_out_3),
    .out_4(contrl_decoder_1_out_4), .out_5(contrl_decoder_1_out_5), .out_6(contrl_decoder_1_out_6),
    .out_7(contrl_decoder_1_out_7), .out_8(contrl_decoder_1_out_8), .out_9(contrl_decoder_1_out_9),
    .out_10(contrl_decoder_1_out_10), .out_11(contrl_decoder_1_out_11), .out_12(contrl_decoder_1_out_12));
  reg_file reg_file_1 (
    .rd(multiplexer_5_out), .in_3(contrl_decoder_1_out_8), .rd_sel(rom_1_data[11:7]), .Reset(button_1_out),
    .read_data1(reg_file_1_read_data1), .read_data_2(reg_file_1_read_data_2), .in_6(clock_1_out),
    .rs2_sel(rom_1_data[24:20]), .rs1_sel(rom_1_data[19:15]));
  Multiplexer #(.select(2), .width(32)) multiplexer_2 (
    .in0(reg_file_1_read_data1), .in1(adder_1_out), .in2(register_1_q), .out(multiplexer_2_out),
    .sel(contrl_decoder_1_out_3));  // open: in3, en
  ALU_controller alu_controller_1 (
    .ALUOP(contrl_decoder_1_out_11), .Func3(rom_1_data[14:12]), .Func7(rom_1_data[30]),
    .out_4(alu_controller_1_out_4));
  Multiplexer #(.width(32)) multiplexer_3 (
    .in0(reg_file_1_read_data_2), .in1(immigiate_1_out_4), .out(multiplexer_3_out),
    .sel(contrl_decoder_1_out_4));  // open: en
  _32_bit_ALU u_32_bit_alu_1 (
    .in_1(multiplexer_2_out), .in_2(multiplexer_3_out), .out_4(n32_bit_alu_1_out_4),
    .in_3(alu_controller_1_out_4));
  branch_ALU branch_alu_1 (
    .in_1(reg_file_1_read_data1), .in_2(reg_file_1_read_data_2), .out_4(branch_alu_1_out_4),
    .in_3(rom_1_data[14:12]));
  RAM #(.addrWidth(10), .dataWidth(32), .bus("separate")) ram_1 (
    .addr(n32_bit_alu_1_out_4[11:2]), .din(reg_file_1_read_data_2), .data(ram_1_data),
    .str(contrl_decoder_1_out_5), .ld(contrl_decoder_1_out_6));  // open: sel, clk, clr
  Multiplexer #(.width(32)) multiplexer_4 (
    .in0(n32_bit_alu_1_out_4), .in1(ram_1_data), .out(multiplexer_4_out), .sel(contrl_decoder_1_out_7));  // open: en
  Multiplexer #(.width(32)) multiplexer_5 (
    .in0(multiplexer_4_out), .in1(adder_1_out), .out(multiplexer_5_out), .sel(contrl_decoder_1_out_12));  // open: en

  // Notes on the sheet:
  //   contents of rom_1 (hex, n*v repeats v):
  //   513 593 500613 c5c463 10000ef 150513 158593 ff1ff0ef
endmodule

module reg_file (
  input  [31:0] rd,
  input  [4:0] rs1_sel,
  input  in_3,
  input  [4:0] rd_sel,
  input  [4:0] rs2_sel,
  input  in_6,
  input  Reset,
  output [31:0] read_data1,
  output [31:0] read_data_2
);

  wire decoder_1_out0, decoder_1_out1, decoder_1_out2, decoder_1_out3, decoder_1_out4, decoder_1_out5,
       decoder_1_out6, decoder_1_out7, decoder_1_out8, decoder_1_out9, decoder_1_out10, decoder_1_out11,
       decoder_1_out12, decoder_1_out13, decoder_1_out14, decoder_1_out15, decoder_1_out16, decoder_1_out17,
       decoder_1_out18, decoder_1_out19, decoder_1_out20, decoder_1_out21, decoder_1_out22, decoder_1_out23,
       decoder_1_out24, decoder_1_out25, decoder_1_out26, decoder_1_out27, decoder_1_out28, decoder_1_out29,
       decoder_1_out30, decoder_1_out31;
  wire [31:0] register_1_q, register_2_q, register_3_q, register_4_q, register_6_q, register_7_q,
       register_8_q, register_9_q, register_10_q, register_11_q, register_12_q, register_13_q, register_14_q,
       register_15_q, register_16_q, register_17_q, register_18_q, register_19_q, register_20_q,
       register_21_q, register_22_q, register_23_q, register_24_q, register_25_q, register_26_q,
       register_27_q, register_28_q, register_29_q, register_30_q, register_31_q, register_32_q, undriven;

  Decoder #(.select(5)) decoder_1 (
    .out0(decoder_1_out0), .out1(decoder_1_out1), .out2(decoder_1_out2), .out3(decoder_1_out3),
    .out4(decoder_1_out4), .out5(decoder_1_out5), .out6(decoder_1_out6), .out7(decoder_1_out7),
    .out8(decoder_1_out8), .out9(decoder_1_out9), .out10(decoder_1_out10), .out11(decoder_1_out11),
    .out12(decoder_1_out12), .out13(decoder_1_out13), .out14(decoder_1_out14), .out15(decoder_1_out15),
    .out16(decoder_1_out16), .out17(decoder_1_out17), .out18(decoder_1_out18), .out19(decoder_1_out19),
    .out20(decoder_1_out20), .out21(decoder_1_out21), .out22(decoder_1_out22), .out23(decoder_1_out23),
    .out24(decoder_1_out24), .out25(decoder_1_out25), .out26(decoder_1_out26), .out27(decoder_1_out27),
    .out28(decoder_1_out28), .out29(decoder_1_out29), .out30(decoder_1_out30), .out31(decoder_1_out31),
    .sel(rd_sel), .en(in_3));
  Register #(.width(32)) register_1 (.D(rd), .en(decoder_1_out0), .Q(register_1_q), .clk(in_6), .clr(Reset));
  Register #(.width(32)) register_2 (.D(rd), .en(decoder_1_out1), .Q(register_2_q), .clk(in_6), .clr(Reset));
  Register #(.width(32)) register_3 (.D(rd), .en(decoder_1_out2), .Q(register_3_q), .clk(in_6), .clr(Reset));
  Register #(.width(32)) register_4 (.D(rd), .en(decoder_1_out3), .Q(register_4_q), .clk(in_6), .clr(Reset));
  Register #(.width(32)) register_5 (.D(rd), .en(decoder_1_out4), .clk(in_6), .clr(Reset));  // open: Q
  Register #(.width(32)) register_6 (.D(rd), .en(decoder_1_out5), .Q(register_6_q), .clk(in_6), .clr(Reset));
  Register #(.width(32)) register_7 (.D(rd), .en(decoder_1_out6), .Q(register_7_q), .clk(in_6), .clr(Reset));
  Register #(.width(32)) register_8 (.D(rd), .en(decoder_1_out7), .Q(register_8_q), .clk(in_6), .clr(Reset));
  Register #(.width(32)) register_9 (.D(rd), .en(decoder_1_out8), .Q(register_9_q), .clk(in_6), .clr(Reset));
  Register #(.width(32)) register_10 (.D(rd), .en(decoder_1_out9), .Q(register_10_q), .clk(in_6), .clr(Reset));
  Register #(.width(32)) register_11 (.D(rd), .en(decoder_1_out10), .Q(register_11_q), .clk(in_6), .clr(Reset));
  Register #(.width(32)) register_12 (.D(rd), .en(decoder_1_out11), .Q(register_12_q), .clk(in_6), .clr(Reset));
  Register #(.width(32)) register_13 (.D(rd), .en(decoder_1_out12), .Q(register_13_q), .clk(in_6), .clr(Reset));
  Register #(.width(32)) register_14 (.D(rd), .en(decoder_1_out13), .Q(register_14_q), .clk(in_6), .clr(Reset));
  Register #(.width(32)) register_15 (.D(rd), .en(decoder_1_out14), .Q(register_15_q), .clk(in_6), .clr(Reset));
  Register #(.width(32)) register_16 (.D(rd), .en(decoder_1_out15), .Q(register_16_q), .clk(in_6), .clr(Reset));
  Register #(.width(32)) register_17 (.D(rd), .en(decoder_1_out16), .Q(register_17_q), .clk(in_6), .clr(Reset));
  Register #(.width(32)) register_18 (.D(rd), .en(decoder_1_out17), .Q(register_18_q), .clk(in_6), .clr(Reset));
  Register #(.width(32)) register_19 (.D(rd), .en(decoder_1_out18), .Q(register_19_q), .clk(in_6), .clr(Reset));
  Register #(.width(32)) register_20 (.D(rd), .en(decoder_1_out19), .Q(register_20_q), .clk(in_6), .clr(Reset));
  Register #(.width(32)) register_21 (.D(rd), .en(decoder_1_out20), .Q(register_21_q), .clk(in_6), .clr(Reset));
  Register #(.width(32)) register_22 (.D(rd), .en(decoder_1_out21), .Q(register_22_q), .clk(in_6), .clr(Reset));
  Register #(.width(32)) register_23 (.D(rd), .en(decoder_1_out22), .Q(register_23_q), .clk(in_6), .clr(Reset));
  Register #(.width(32)) register_24 (.D(rd), .en(decoder_1_out23), .Q(register_24_q), .clk(in_6), .clr(Reset));
  Register #(.width(32)) register_25 (.D(rd), .en(decoder_1_out24), .Q(register_25_q), .clk(in_6), .clr(Reset));
  Register #(.width(32)) register_26 (.D(rd), .en(decoder_1_out25), .Q(register_26_q), .clk(in_6), .clr(Reset));
  Register #(.width(32)) register_27 (.D(rd), .en(decoder_1_out26), .Q(register_27_q), .clk(in_6), .clr(Reset));
  Register #(.width(32)) register_28 (.D(rd), .en(decoder_1_out27), .Q(register_28_q), .clk(in_6), .clr(Reset));
  Register #(.width(32)) register_29 (.D(rd), .en(decoder_1_out28), .Q(register_29_q), .clk(in_6), .clr(Reset));
  Register #(.width(32)) register_30 (.D(rd), .en(decoder_1_out29), .Q(register_30_q), .clk(in_6), .clr(Reset));
  Register #(.width(32)) register_31 (.D(rd), .en(decoder_1_out30), .Q(register_31_q), .clk(in_6), .clr(Reset));
  Register #(.width(32)) register_32 (.D(rd), .en(decoder_1_out31), .Q(register_32_q), .clk(in_6), .clr(Reset));
  Multiplexer #(.select(5), .width(32)) multiplexer_1 (
    .in0(register_1_q), .in1(register_2_q), .in2(register_3_q), .in3(register_4_q), .in4(undriven),
    .in5(register_6_q), .in6(register_7_q), .in7(register_8_q), .in8(register_9_q), .in9(register_10_q),
    .in10(register_11_q), .in11(register_12_q), .in12(register_13_q), .in13(register_14_q),
    .in14(register_15_q), .in15(register_16_q), .in16(register_17_q), .in17(register_18_q),
    .in18(register_19_q), .in19(register_20_q), .in20(register_21_q), .in21(register_22_q),
    .in22(register_23_q), .in23(register_24_q), .in24(register_25_q), .in25(register_26_q),
    .in26(register_27_q), .in27(register_28_q), .in28(register_29_q), .in29(register_30_q),
    .in30(register_31_q), .in31(register_32_q), .out(read_data1), .sel(rs1_sel));  // open: en
  Multiplexer #(.select(5), .width(32)) multiplexer_2 (
    .in0(register_1_q), .in1(register_2_q), .in2(register_3_q), .in3(register_4_q), .in4(undriven),
    .in5(register_6_q), .in6(register_7_q), .in7(register_8_q), .in8(register_9_q), .in9(register_10_q),
    .in10(register_11_q), .in11(register_12_q), .in12(register_13_q), .in13(register_14_q),
    .in14(register_15_q), .in15(register_16_q), .in16(register_17_q), .in17(register_18_q),
    .in18(register_19_q), .in19(register_20_q), .in20(register_21_q), .in21(register_22_q),
    .in22(register_24_q), .in23(register_25_q), .in24(register_26_q), .in25(register_27_q),
    .in26(register_28_q), .in27(register_29_q), .in28(register_30_q), .in29(register_31_q),
    .in30(register_32_q), .out(read_data_2), .sel(rs2_sel));  // open: in31, en

  // Notes on the sheet:
  //   Clock
endmodule

module contrl_decoder (
  input  [6:0] in_1,
  input  in_2,
  output [1:0] out_3,
  output out_4,
  output out_5,
  output out_6,
  output out_7,
  output out_8,
  output [1:0] out_9,
  output [1:0] out_10,
  output [2:0] out_11,
  output out_12
);

  wire and_1_out, decoder_1_addi, decoder_1_auipc, decoder_1_b, decoder_1_i_type, decoder_1_jal,
       decoder_1_jalr, decoder_1_lui, decoder_1_out_2, decoder_1_out_4;

  decoder decoder_1 (
    .in_1(in_1), .out_2(decoder_1_out_2), .addi(decoder_1_addi), .out_4(decoder_1_out_4), .B(decoder_1_b),
    .Jalr(decoder_1_jalr), .I_type(decoder_1_i_type), .LUI(decoder_1_lui), .auipc(decoder_1_auipc),
    .jal(decoder_1_jal));
  and and_1 (and_1_out, decoder_1_b, in_2);
  controller controller_1 (
    .R(decoder_1_out_2), .I(decoder_1_addi), .S(decoder_1_out_4), .B(and_1_out), .LUI(decoder_1_lui),
    .Auipc(decoder_1_auipc), .Jal(decoder_1_jal), .Jalr(decoder_1_jalr), .Lw(decoder_1_i_type),
    .OpB_sel(out_4), .Mem_write(out_5), .out_13(out_6), .out_14(out_7), .out_15(out_8), .ALUOP(out_11),
    .JALR_2(out_12), .Pc_sel(out_9), .Imm_sel(out_10), .OpA_sel(out_3));

  // Notes on the sheet:
  //   DECODER
  //   CONTROL DECODER
endmodule

module decoder (
  input  [6:0] in_1,
  output out_2,
  output addi,
  output out_4,
  output B,
  output Jalr,
  output I_type,
  output LUI,
  output auipc,
  output jal
);

  Comparator #(.width(7)) comparator_1 (.a(7'b0110011), .b(in_1), .eq(out_2));  // open: gt, lt
  Comparator #(.width(7)) comparator_2 (.a(7'b0010011), .b(in_1), .eq(addi));  // open: gt, lt
  Comparator #(.width(7)) comparator_3 (.a(7'b0100011), .b(in_1), .eq(out_4));  // open: gt, lt
  Comparator #(.width(7)) comparator_4 (.a(7'b1100011), .b(in_1), .eq(B));  // open: gt, lt
  Comparator #(.width(7)) comparator_5 (.a(7'b1100111), .b(in_1), .eq(Jalr));  // open: gt, lt
  Comparator #(.width(7)) comparator_6 (.a(7'b0000011), .b(in_1), .eq(I_type));  // open: gt, lt
  Comparator #(.width(7)) comparator_7 (.a(7'b0110111), .b(in_1), .eq(LUI));  // open: gt, lt
  Comparator #(.width(7)) comparator_8 (.a(7'b0010111), .b(in_1), .eq(auipc));  // open: gt, lt
  Comparator #(.width(7)) comparator_9 (.a(7'b1101111), .b(in_1), .eq(jal));  // open: gt, lt

  // Notes on the sheet:
  //   opcode in hexa decimal
  //   R
  //   I
  //   S
  //   Lw
endmodule

module controller (
  input  R,
  input  I,
  input  S,
  input  B,
  input  LUI,
  input  Auipc,
  input  Jal,
  input  Jalr,
  input  Lw,
  output [1:0] OpA_sel,
  output OpB_sel,
  output Mem_write,
  output out_13,
  output out_14,
  output out_15,
  output [1:0] Pc_sel,
  output [1:0] Imm_sel,
  output [2:0] ALUOP,
  output JALR_2
);

  wire and_1_out, and_2_out, and_3_out, and_4_out, not_1_out, not_2_out, not_3_out, not_4_out, not_5_out,
       not_6_out, not_7_out, not_8_out;

  OpA_sel opa_sel_1 (.LUI(LUI), .AUIPC(Auipc), .JAL(Jal), .out_4(OpA_sel));
  or or_1 (OpB_sel, I, S, LUI, Auipc, Jalr, Lw);
  not not_1 (not_1_out, B);
  not not_2 (not_2_out, Jal);
  not not_3 (not_3_out, B);
  not not_4 (not_4_out, Jalr);
  not not_5 (not_5_out, B);
  not not_6 (not_6_out, Jal);
  not not_7 (not_7_out, Jal);
  not not_8 (not_8_out, Jalr);
  imm_sel imm_sel_1 (.R(R), .S(S), .B(B), .lui(LUI), .auiPC(Auipc), .JAL(Jal), .out_7(Imm_sel));
  ALUOP aluop_1 (.R(R), .I(I), .S(S), .LUI(LUI), .AUIPC(Auipc), .LW(Lw), .JALR(Jalr), .JAL(Jal), .out_9(ALUOP));
  or or_2 (out_15, R, I, LUI, Auipc, Jal, Jalr, Lw);
  and and_1 (and_1_out, not_1_out, not_2_out, Jalr);
  or or_3 (Pc_sel[1], and_1_out, and_2_out);
  and and_2 (and_2_out, not_3_out, Jal, not_4_out);
  and and_3 (and_3_out, not_5_out, not_6_out, Jalr);
  or or_4 (Pc_sel[0], and_3_out, and_4_out);
  and and_4 (and_4_out, B, not_7_out, not_8_out);

  assign JALR_2 = Jalr;
  assign Mem_write = S;
  assign out_13 = Lw;
  assign out_14 = Lw;

  // Notes on the sheet:
  //   Mem_read
  //   Write_back
  //   regfile_en
endmodule

module ALUOP (
  input  R,
  input  I,
  input  S,
  input  LUI,
  input  AUIPC,
  input  LW,
  input  JALR,
  input  JAL,
  output [2:0] out_9
);

  wire and_1_out, and_2_out, and_3_out, and_4_out, and_5_out, and_6_out, and_7_out, and_8_out, and_9_out,
       and_10_out, and_11_out, and_12_out, and_13_out, and_14_out, and_15_out, and_16_out, and_17_out,
       and_18_out, and_19_out, and_20_out, and_21_out, and_22_out, and_23_out, and_24_out, and_25_out,
       and_26_out, and_27_out, and_28_out, and_29_out, and_30_out, and_31_out, and_32_out, and_33_out,
       and_34_out, and_35_out, and_36_out, and_37_out, and_38_out, and_39_out, and_40_out, and_41_out,
       and_42_out, and_43_out, and_44_out, and_45_out, and_46_out, and_47_out, and_48_out, and_49_out,
       and_50_out, and_51_out, and_52_out, and_53_out, and_54_out, and_55_out, and_56_out, and_57_out,
       and_58_out, and_59_out, and_60_out, and_61_out, and_62_out, and_63_out, and_64_out, and_65_out,
       and_66_out, and_67_out, and_68_out, and_69_out, and_70_out, and_71_out, and_72_out, and_73_out,
       and_74_out, and_75_out, and_76_out, and_77_out, and_78_out, and_79_out, and_80_out, and_81_out,
       and_82_out, and_83_out, and_84_out, not_1_out, not_2_out, not_3_out, not_4_out, not_5_out, not_6_out,
       not_7_out, not_8_out, not_9_out, not_10_out, not_11_out, not_12_out, not_13_out, not_14_out,
       not_15_out, not_16_out, not_17_out, not_18_out, not_19_out, not_20_out, not_21_out, not_22_out,
       not_23_out, not_24_out, not_25_out, not_26_out, not_27_out, not_28_out, not_29_out, not_30_out,
       not_31_out, not_32_out, not_33_out, not_34_out, not_35_out, not_36_out, not_37_out, not_38_out,
       not_39_out, not_40_out, not_41_out, not_42_out, not_43_out, not_44_out, not_45_out, not_46_out,
       not_47_out, not_48_out, not_49_out, not_50_out, not_51_out, not_52_out, not_53_out, not_54_out,
       not_55_out, not_56_out, not_57_out, not_58_out, not_59_out, not_60_out, not_61_out, not_62_out,
       not_63_out, not_64_out, not_65_out, not_66_out, not_67_out, not_68_out, not_69_out, not_70_out,
       not_71_out, not_72_out, not_73_out, not_74_out, not_75_out, not_76_out, not_77_out, not_78_out,
       not_79_out, not_80_out, not_81_out, not_82_out, not_83_out, not_84_out, or_1_out, or_2_out, or_3_out,
       or_4_out, or_5_out, or_6_out;

  not not_1 (not_1_out, R);
  and and_1 (and_1_out, not_1_out, not_2_out);
  not not_2 (not_2_out, I);
  not not_3 (not_3_out, S);
  and and_2 (and_2_out, not_3_out, not_4_out);
  not not_4 (not_4_out, LUI);
  not not_5 (not_5_out, AUIPC);
  and and_3 (and_3_out, not_5_out, not_6_out);
  not not_6 (not_6_out, LW);
  not not_7 (not_7_out, JALR);
  and and_4 (and_4_out, not_7_out, JAL);
  not not_8 (not_8_out, R);
  and and_5 (and_5_out, not_8_out, not_9_out);
  not not_9 (not_9_out, I);
  not not_10 (not_10_out, S);
  and and_6 (and_6_out, not_10_out, not_11_out);
  not not_11 (not_11_out, LUI);
  and and_7 (and_7_out, AUIPC, not_12_out);
  not not_12 (not_12_out, LW);
  not not_13 (not_13_out, JALR);
  and and_8 (and_8_out, not_13_out, not_14_out);
  not not_14 (not_14_out, JAL);
  not not_15 (not_15_out, R);
  and and_9 (and_9_out, not_15_out, not_16_out);
  not not_16 (not_16_out, I);
  not not_17 (not_17_out, S);
  and and_10 (and_10_out, not_17_out, LUI);
  not not_18 (not_18_out, AUIPC);
  and and_11 (and_11_out, not_18_out, not_19_out);
  not not_19 (not_19_out, LW);
  not not_20 (not_20_out, JALR);
  and and_12 (and_12_out, not_20_out, not_21_out);
  not not_21 (not_21_out, JAL);
  not not_22 (not_22_out, R);
  and and_13 (and_13_out, not_22_out, not_23_out);
  not not_23 (not_23_out, I);
  and and_14 (and_14_out, S, not_24_out);
  not not_24 (not_24_out, LUI);
  not not_25 (not_25_out, AUIPC);
  and and_15 (and_15_out, not_25_out, not_26_out);
  not not_26 (not_26_out, LW);
  not not_27 (not_27_out, JALR);
  and and_16 (and_16_out, not_27_out, not_28_out);
  not not_28 (not_28_out, JAL);
  not not_29 (not_29_out, R);
  and and_17 (and_17_out, not_29_out, not_30_out);
  not not_30 (not_30_out, I);
  not not_31 (not_31_out, S);
  and and_18 (and_18_out, not_31_out, not_32_out);
  not not_32 (not_32_out, LUI);
  not not_33 (not_33_out, AUIPC);
  and and_19 (and_19_out, not_33_out, not_34_out);
  not not_34 (not_34_out, LW);
  not not_35 (not_35_out, JALR);
  and and_20 (and_20_out, not_35_out, JAL);
  not not_36 (not_36_out, R);
  and and_21 (and_21_out, not_36_out, not_37_out);
  not not_37 (not_37_out, I);
  not not_38 (not_38_out, S);
  and and_22 (and_22_out, not_38_out, not_39_out);
  not not_39 (not_39_out, LUI);
  not not_40 (not_40_out, AUIPC);
  and and_23 (and_23_out, not_40_out, not_41_out);
  not not_41 (not_41_out, LW);
  and and_24 (and_24_out, JALR, not_42_out);
  not not_42 (not_42_out, JAL);
  not not_43 (not_43_out, R);
  and and_25 (and_25_out, not_43_out, not_44_out);
  not not_44 (not_44_out, I);
  not not_45 (not_45_out, S);
  and and_26 (and_26_out, not_45_out, LUI);
  not not_46 (not_46_out, AUIPC);
  and and_27 (and_27_out, not_46_out, not_47_out);
  not not_47 (not_47_out, LW);
  not not_48 (not_48_out, JALR);
  and and_28 (and_28_out, not_48_out, not_49_out);
  not not_49 (not_49_out, JAL);
  not not_50 (not_50_out, R);
  and and_29 (and_29_out, not_50_out, I);
  not not_51 (not_51_out, S);
  and and_30 (and_30_out, not_51_out, not_52_out);
  not not_52 (not_52_out, LUI);
  not not_53 (not_53_out, AUIPC);
  and and_31 (and_31_out, not_53_out, not_54_out);
  not not_54 (not_54_out, LW);
  not not_55 (not_55_out, JALR);
  and and_32 (and_32_out, not_55_out, not_56_out);
  not not_56 (not_56_out, JAL);
  not not_57 (not_57_out, R);
  and and_33 (and_33_out, not_57_out, not_58_out);
  not not_58 (not_58_out, I);
  not not_59 (not_59_out, S);
  and and_34 (and_34_out, not_59_out, not_60_out);
  not not_60 (not_60_out, LUI);
  not not_61 (not_61_out, AUIPC);
  and and_35 (and_35_out, not_61_out, not_62_out);
  not not_62 (not_62_out, LW);
  not not_63 (not_63_out, JALR);
  and and_36 (and_36_out, not_63_out, JAL);
  not not_64 (not_64_out, R);
  and and_37 (and_37_out, not_64_out, not_65_out);
  not not_65 (not_65_out, I);
  not not_66 (not_66_out, S);
  and and_38 (and_38_out, not_66_out, not_67_out);
  not not_67 (not_67_out, LUI);
  not not_68 (not_68_out, AUIPC);
  and and_39 (and_39_out, not_68_out, not_69_out);
  not not_69 (not_69_out, LW);
  and and_40 (and_40_out, JALR, not_70_out);
  not not_70 (not_70_out, JAL);
  not not_71 (not_71_out, R);
  and and_41 (and_41_out, not_71_out, not_72_out);
  not not_72 (not_72_out, I);
  not not_73 (not_73_out, S);
  and and_42 (and_42_out, not_73_out, not_74_out);
  not not_74 (not_74_out, LUI);
  not not_75 (not_75_out, AUIPC);
  and and_43 (and_43_out, not_75_out, LW);
  not not_76 (not_76_out, JALR);
  and and_44 (and_44_out, not_76_out, not_77_out);
  not not_77 (not_77_out, JAL);
  not not_78 (not_78_out, R);
  and and_45 (and_45_out, not_78_out, not_79_out);
  not not_79 (not_79_out, I);
  not not_80 (not_80_out, S);
  and and_46 (and_46_out, not_80_out, not_81_out);
  not not_81 (not_81_out, LUI);
  and and_47 (and_47_out, AUIPC, not_82_out);
  not not_82 (not_82_out, LW);
  not not_83 (not_83_out, JALR);
  and and_48 (and_48_out, not_83_out, not_84_out);
  not not_84 (not_84_out, JAL);
  and and_49 (and_49_out, and_1_out, and_2_out);
  and and_50 (and_50_out, and_3_out, and_4_out);
  and and_51 (and_51_out, and_5_out, and_6_out);
  and and_52 (and_52_out, and_7_out, and_8_out);
  and and_53 (and_53_out, and_9_out, and_10_out);
  and and_54 (and_54_out, and_11_out, and_12_out);
  and and_55 (and_55_out, and_13_out, and_14_out);
  and and_56 (and_56_out, and_15_out, and_16_out);
  and and_57 (and_57_out, and_17_out, and_18_out);
  and and_58 (and_58_out, and_19_out, and_20_out);
  and and_59 (and_59_out, and_21_out, and_22_out);
  and and_60 (and_60_out, and_23_out, and_24_out);
  and and_61 (and_61_out, and_25_out, and_26_out);
  and and_62 (and_62_out, and_27_out, and_28_out);
  and and_63 (and_63_out, and_29_out, and_30_out);
  and and_64 (and_64_out, and_31_out, and_32_out);
  and and_65 (and_65_out, and_33_out, and_34_out);
  and and_66 (and_66_out, and_35_out, and_36_out);
  and and_67 (and_67_out, and_37_out, and_38_out);
  and and_68 (and_68_out, and_39_out, and_40_out);
  and and_69 (and_69_out, and_41_out, and_42_out);
  and and_70 (and_70_out, and_43_out, and_44_out);
  and and_71 (and_71_out, and_45_out, and_46_out);
  and and_72 (and_72_out, and_47_out, and_48_out);
  and and_73 (and_73_out, and_49_out, and_50_out);
  and and_74 (and_74_out, and_51_out, and_52_out);
  and and_75 (and_75_out, and_53_out, and_54_out);
  and and_76 (and_76_out, and_55_out, and_56_out);
  and and_77 (and_77_out, and_57_out, and_58_out);
  and and_78 (and_78_out, and_59_out, and_60_out);
  and and_79 (and_79_out, and_61_out, and_62_out);
  and and_80 (and_80_out, and_63_out, and_64_out);
  and and_81 (and_81_out, and_65_out, and_66_out);
  and and_82 (and_82_out, and_67_out, and_68_out);
  and and_83 (and_83_out, and_69_out, and_70_out);
  and and_84 (and_84_out, and_71_out, and_72_out);
  or or_1 (or_1_out, and_73_out, and_74_out);
  or or_2 (or_2_out, and_75_out, and_76_out);
  or or_3 (or_3_out, and_77_out, and_78_out);
  or or_4 (or_4_out, and_79_out, and_80_out);
  or or_5 (or_5_out, and_81_out, and_82_out);
  or or_6 (or_6_out, and_83_out, and_84_out);
  or or_7 (out_9[2], or_1_out, or_2_out);
  or or_8 (out_9[1], or_3_out, or_4_out);
  or or_9 (out_9[0], or_5_out, or_6_out);
endmodule

module immigiate (
  input  [31:0] in_1,
  input  [1:0] in_2,
  input  [31:0] in_3,
  output [31:0] out_4,
  output [31:0] out_5,
  output [31:0] out_6
);

  wire [19:0] bit_extender_1_out;

  assign bit_extender_1_out = {{19{1'b0}}, in_1[31]};  // Bit_Extender bit_extender_1
  Adder #(.width(32)) adder_1 (
    .a(in_3), .b({bit_extender_1_out[18:0], in_1[31], in_1[7], in_1[30:25], in_1[11:8], 1'b0}), .out(out_5));  // open: cin, cout
  Adder #(.width(32)) adder_2 (
    .a(in_3), .b({bit_extender_1_out[10:0], in_1[31], in_1[19:12], in_1[20], in_1[30:21], 1'b0}), .out(out_6));  // open: cin, cout
  Multiplexer #(.select(2), .width(32)) multiplexer_1 (
    .in0({bit_extender_1_out, in_1[31:20]}), .in1({bit_extender_1_out, in_1[31:25], in_1[11:7]}),
    .in2({in_1[31:12], {12{1'b0}}}), .out(out_4), .sel(in_2));  // open: in3, en

  // Notes on the sheet:
  //   Instruction
  //   Pc
  //   last bit
  //   I_TYPE
  //   S_TYPE
  //   B_TYPE
  //   U_TYPE
  //   J_TYPE
endmodule

module branch_ALU (
  input  [31:0] in_1,
  input  [31:0] in_2,
  input  [2:0] in_3,
  output out_4
);

  wire comparator_1_eq, comparator_1_gt, comparator_1_lt, comparator_2_eq, comparator_2_gt, comparator_2_lt,
       not_1_out, or_1_out, or_2_out;

  Comparator #(.width(32)) comparator_1 (
    .a(in_1), .b(in_2), .gt(comparator_1_gt), .eq(comparator_1_eq), .lt(comparator_1_lt));
  Comparator #(.width(32), .mode("unsigned")) comparator_2 (
    .a(in_1), .b(in_2), .gt(comparator_2_gt), .eq(comparator_2_eq), .lt(comparator_2_lt));
  not not_1 (not_1_out, comparator_1_eq);
  or or_1 (or_1_out, comparator_1_gt, comparator_1_eq);
  or or_2 (or_2_out, comparator_2_gt, comparator_2_eq);
  Multiplexer #(.select(3)) multiplexer_1 (
    .in0(comparator_1_eq), .in1(not_1_out), .in4(comparator_1_lt), .in5(or_1_out), .in6(comparator_2_lt),
    .in7(or_2_out), .out(out_4), .sel(in_3));  // open: in2, in3, en

  // Notes on the sheet:
  //   bge
  //   beq
  //   blt
  //   bne
  //   bgeu
  //   bltu
endmodule

module _32_bit_ALU (
  input  [31:0] in_1,
  input  [31:0] in_2,
  input  [3:0] in_3,
  output [31:0] out_4
);

  wire comparator_1_eq, comparator_2_lt, comparator_3_gt;
  wire [31:0] adder_1_out, and_1_out, multiplexer_1_out, multiplexer_2_out, multiplexer_3_out, or_1_out,
       shifter_1_out, shifter_2_out, shifter_3_out, subtractor_1_out, xor_1_out;

  Adder #(.width(32)) adder_1 (.a(in_1), .b(in_2), .out(adder_1_out));  // open: cin, cout
  Subtractor #(.width(32)) subtractor_1 (.a(in_1), .b(in_2), .out(subtractor_1_out));  // open: bin, bout
  Shifter #(.width(32)) shifter_1 (.in(in_1), .\dist (in_2[4:0]), .out(shifter_1_out));
  Shifter #(.width(32), .shift("lr")) shifter_2 (.in(in_1), .\dist (in_2[4:0]), .out(shifter_2_out));
  Shifter #(.width(32), .shift("ar")) shifter_3 (.in(in_1), .\dist (in_2[4:0]), .out(shifter_3_out));
  Comparator #(.width(32)) comparator_1 (.a(in_1), .b(in_2), .eq(comparator_1_eq));  // open: gt, lt
  Comparator #(.width(32)) comparator_2 (.a(in_1), .b(in_2), .lt(comparator_2_lt));  // open: gt, eq
  Comparator #(.width(32)) comparator_3 (.a(in_1), .b(in_2), .gt(comparator_3_gt));  // open: eq, lt
  assign and_1_out = in_1 & in_2;  // AND_Gate and_1, 32 bits wide
  assign or_1_out = in_1 | in_2;  // OR_Gate or_1, 32 bits wide
  assign xor_1_out = in_1 ^ in_2;  // XOR_Gate xor_1, 32 bits wide
  Multiplexer #(.width(32)) multiplexer_1 (
    .in0({32{1'b0}}), .in1(32'h1), .out(multiplexer_1_out), .sel(comparator_1_eq));  // open: en
  Multiplexer #(.width(32)) multiplexer_2 (
    .in0({32{1'b0}}), .in1(32'h1), .out(multiplexer_2_out), .sel(comparator_2_lt));  // open: en
  Multiplexer #(.width(32)) multiplexer_3 (
    .in0({32{1'b0}}), .in1(32'h1), .out(multiplexer_3_out), .sel(comparator_3_gt));  // open: en
  Multiplexer #(.select(4), .width(32)) multiplexer_4 (
    .in0(adder_1_out), .in1(subtractor_1_out), .in2(shifter_1_out), .in3(shifter_2_out), .in4(shifter_3_out),
    .in5(multiplexer_1_out), .in6(multiplexer_2_out), .in10(multiplexer_3_out), .in11(and_1_out),
    .in12(and_1_out), .in13(or_1_out), .in14(xor_1_out), .out(out_4), .sel(in_3));  // open: in7, in8, in9, in15, en
endmodule

module program_counter (
  output [31:0] out_1
);

  wire button_1_out, clock_1_out;
  wire [31:0] adder_1_out, register_1_q;

  Clock clock_1 (.out(clock_1_out));
  Register #(.width(32)) register_1 (
    .D(adder_1_out), .Q(register_1_q), .clk(clock_1_out), .clr(button_1_out));  // open: en
  Button button_1 (.out(button_1_out));
  Adder #(.width(32)) adder_1 (.a(register_1_q), .b(32'h4), .out(adder_1_out));  // open: cin, cout
  ROM #(.addrWidth(10), .dataWidth(32)) rom_1 (.addr(register_1_q[11:2]), .data(out_1));  // open: sel

  // Notes on the sheet:
  //   contents of rom_1 (hex, n*v repeats v):
  //   300513 400593 b50633
endmodule

module ALU_controller (
  input  [2:0] ALUOP,
  input  [2:0] Func3,
  input  Func7,
  output [3:0] out_4
);

  wire and_1_out, and_2_out, and_3_out, and_4_out, and_5_out, and_6_out, and_7_out, and_8_out, and_9_out,
       and_10_out, and_11_out, and_12_out, and_13_out, and_14_out, and_15_out, and_16_out, and_17_out,
       and_18_out, and_19_out, and_20_out, and_21_out, and_22_out, and_23_out, and_24_out, and_25_out,
       and_26_out, and_27_out, and_28_out, and_29_out, and_30_out, and_31_out, not_1_out, not_2_out,
       not_3_out, not_4_out, not_5_out, not_6_out, not_7_out, not_8_out, not_9_out, not_10_out, not_11_out,
       not_12_out, not_13_out, not_14_out, not_15_out, not_16_out, not_17_out, not_18_out, not_19_out,
       not_20_out, not_21_out, not_22_out, not_23_out, not_24_out, or_2_out, or_3_out, or_4_out, or_7_out,
       or_8_out, or_9_out;

  not not_1 (not_1_out, ALUOP[2]);
  not not_2 (not_2_out, ALUOP[0]);
  not not_3 (not_3_out, Func3[0]);
  not not_4 (not_4_out, ALUOP[0]);
  not not_5 (not_5_out, Func3[1]);
  not not_6 (not_6_out, ALUOP[0]);
  not not_7 (not_7_out, ALUOP[0]);
  not not_8 (not_8_out, Func3[0]);
  not not_9 (not_9_out, Func3[1]);
  not not_10 (not_10_out, ALUOP[0]);
  not not_11 (not_11_out, Func3[1]);
  not not_12 (not_12_out, ALUOP[0]);
  not not_13 (not_13_out, ALUOP[1]);
  not not_14 (not_14_out, ALUOP[0]);
  and and_1 (and_1_out, not_1_out, not_2_out);
  and and_2 (and_2_out, and_1_out, and_3_out);
  and and_3 (and_3_out, not_3_out, Func3[1]);
  and and_4 (and_4_out, ALUOP[2], ALUOP[1]);
  and and_5 (and_5_out, not_4_out, not_5_out);
  and and_6 (and_6_out, and_5_out, Func3[2]);
  and and_7 (and_7_out, not_6_out, Func3[0]);
  and and_8 (and_8_out, and_7_out, not_15_out);
  not not_15 (not_15_out, Func3[1]);
  and and_9 (and_9_out, not_7_out, not_8_out);
  and and_10 (and_10_out, and_9_out, and_11_out);
  and and_11 (and_11_out, not_9_out, Func3[2]);
  and and_12 (and_12_out, not_10_out, not_11_out);
  and and_13 (and_13_out, and_12_out, and_14_out);
  and and_14 (and_14_out, Func3[2], Func7);
  and and_15 (and_15_out, not_12_out, Func3[0]);
  and and_16 (and_16_out, and_15_out, Func3[1]);
  and and_17 (and_17_out, ALUOP[2], ALUOP[1]);
  and and_18 (and_18_out, not_13_out, not_14_out);
  and and_19 (and_19_out, and_18_out, not_16_out);
  not not_16 (not_16_out, Func3[0]);
  not not_17 (not_17_out, Func3[1]);
  and and_20 (and_20_out, not_17_out, Func7);
  not not_18 (not_18_out, ALUOP[2]);
  and and_21 (and_21_out, not_18_out, not_19_out);
  not not_19 (not_19_out, Func3[0]);
  not not_20 (not_20_out, ALUOP[2]);
  not not_21 (not_21_out, Func3[1]);
  not not_22 (not_22_out, Func7);
  not not_23 (not_23_out, ALUOP[2]);
  not not_24 (not_24_out, Func3[2]);
  or or_1 (out_4[3], and_2_out, and_4_out);
  or or_2 (or_2_out, and_6_out, and_8_out);
  and and_22 (and_22_out, ALUOP[2], ALUOP[1]);
  or or_3 (or_3_out, and_10_out, and_13_out);
  or or_4 (or_4_out, and_16_out, and_17_out);
  and and_23 (and_23_out, and_19_out, and_20_out);
  and and_24 (and_24_out, and_21_out, Func3[2]);
  and and_25 (and_25_out, not_20_out, not_21_out);
  and and_26 (and_26_out, Func3[2], not_22_out);
  and and_27 (and_27_out, not_23_out, Func3[0]);
  and and_28 (and_28_out, Func3[1], not_24_out);
  or or_5 (out_4[2], or_2_out, and_22_out);
  or or_6 (out_4[1], or_3_out, or_4_out);
  or or_7 (or_7_out, and_23_out, and_24_out);
  and and_29 (and_29_out, and_25_out, and_26_out);
  and and_30 (and_30_out, and_27_out, and_28_out);
  and and_31 (and_31_out, ALUOP[1], ALUOP[0]);
  or or_8 (or_8_out, or_7_out, and_29_out);
  or or_9 (or_9_out, and_30_out, and_31_out);
  or or_10 (out_4[0], or_8_out, or_9_out);

  // Notes on the sheet:
  //   AluOp2
  //   AluOp1
  //   AluOp0
  //   Func2
  //   Func1
  //   Func0
  //   OUT3
  //   OUT2
  //   OUT1
  //   OUT0
endmodule

module imm_sel (
  input  R,
  input  S,
  input  B,
  input  lui,
  input  auiPC,
  input  JAL,
  output [1:0] out_7
);

  wire and_1_out, and_2_out, and_3_out, and_4_out, and_5_out, and_6_out, and_7_out, and_8_out, and_9_out,
       not_1_out, not_2_out, not_3_out, not_4_out, not_5_out, not_6_out, not_7_out, not_8_out, not_9_out,
       not_10_out, not_11_out, not_12_out, not_13_out, not_14_out, not_15_out, not_16_out, not_17_out,
       not_18_out, not_19_out, not_20_out, not_21_out, not_22_out, not_23_out, not_24_out, not_25_out,
       not_26_out, not_27_out, not_28_out, not_29_out, not_30_out, not_31_out, not_32_out, not_33_out,
       not_34_out, not_35_out, not_36_out, not_37_out, not_38_out, not_39_out, not_40_out, not_41_out,
       not_42_out, not_43_out, not_44_out, not_45_out;

  not not_1 (not_1_out, R);
  not not_2 (not_2_out, S);
  not not_3 (not_3_out, B);
  not not_4 (not_4_out, lui);
  not not_5 (not_5_out, auiPC);
  not not_6 (not_6_out, R);
  not not_7 (not_7_out, S);
  not not_8 (not_8_out, B);
  not not_9 (not_9_out, lui);
  not not_10 (not_10_out, JAL);
  not not_11 (not_11_out, R);
  not not_12 (not_12_out, S);
  not not_13 (not_13_out, B);
  not not_14 (not_14_out, auiPC);
  not not_15 (not_15_out, JAL);
  not not_16 (not_16_out, R);
  not not_17 (not_17_out, S);
  not not_18 (not_18_out, lui);
  not not_19 (not_19_out, auiPC);
  not not_20 (not_20_out, JAL);
  not not_21 (not_21_out, S);
  not not_22 (not_22_out, B);
  not not_23 (not_23_out, lui);
  not not_24 (not_24_out, auiPC);
  not not_25 (not_25_out, JAL);
  not not_26 (not_26_out, R);
  not not_27 (not_27_out, S);
  not not_28 (not_28_out, B);
  not not_29 (not_29_out, lui);
  not not_30 (not_30_out, auiPC);
  not not_31 (not_31_out, R);
  not not_32 (not_32_out, S);
  not not_33 (not_33_out, lui);
  not not_34 (not_34_out, auiPC);
  not not_35 (not_35_out, JAL);
  not not_36 (not_36_out, R);
  not not_37 (not_37_out, B);
  not not_38 (not_38_out, lui);
  not not_39 (not_39_out, auiPC);
  not not_40 (not_40_out, JAL);
  not not_41 (not_41_out, S);
  not not_42 (not_42_out, B);
  not not_43 (not_43_out, lui);
  not not_44 (not_44_out, auiPC);
  not not_45 (not_45_out, JAL);
  and and_1 (and_1_out, not_1_out, not_2_out, not_3_out, not_4_out, not_5_out, JAL);
  and and_2 (and_2_out, not_6_out, not_7_out, not_8_out, not_9_out, auiPC, not_10_out);
  and and_3 (and_3_out, not_11_out, not_12_out, not_13_out, lui, not_14_out, not_15_out);
  and and_4 (and_4_out, not_16_out, not_17_out, B, not_18_out, not_19_out, not_20_out);
  and and_5 (and_5_out, R, not_21_out, not_22_out, not_23_out, not_24_out, not_25_out);
  and and_6 (and_6_out, not_26_out, not_27_out, not_28_out, not_29_out, not_30_out, JAL);
  and and_7 (and_7_out, not_31_out, not_32_out, B, not_33_out, not_34_out, not_35_out);
  and and_8 (and_8_out, not_36_out, S, not_37_out, not_38_out, not_39_out, not_40_out);
  and and_9 (and_9_out, R, not_41_out, not_42_out, not_43_out, not_44_out, not_45_out);
  or or_1 (out_7[1], and_1_out, and_2_out, and_3_out, and_4_out, and_5_out);
  or or_2 (out_7[0], and_6_out, and_7_out, and_8_out, and_9_out);
endmodule

module OpA_sel (
  input  LUI,
  input  AUIPC,
  input  JAL,
  output [1:0] out_4
);

  wire and_1_out, and_2_out, and_3_out, and_4_out, and_5_out, and_6_out, and_7_out, and_8_out, not_1_out,
       not_2_out, not_3_out, not_4_out, not_5_out, not_6_out, not_7_out, not_8_out;

  not not_1 (not_1_out, LUI);
  not not_2 (not_2_out, AUIPC);
  not not_3 (not_3_out, AUIPC);
  not not_4 (not_4_out, LUI);
  not not_5 (not_5_out, AUIPC);
  and and_1 (and_1_out, not_1_out, not_2_out);
  and and_2 (and_2_out, LUI, not_3_out);
  not not_6 (not_6_out, JAL);
  and and_3 (and_3_out, not_4_out, AUIPC);
  not not_7 (not_7_out, JAL);
  and and_4 (and_4_out, LUI, not_5_out);
  not not_8 (not_8_out, JAL);
  and and_5 (and_5_out, and_1_out, JAL);
  and and_6 (and_6_out, and_2_out, not_6_out);
  and and_7 (and_7_out, and_3_out, not_7_out);
  and and_8 (and_8_out, and_4_out, not_8_out);
  or or_1 (out_4[1], and_5_out, and_6_out);
  or or_2 (out_4[0], and_7_out, and_8_out);
endmodule
